// Logisim project Exercicios em sala 08_15_24.circ as structural Verilog: 3 circuits, main circuit main
module main (
);

  wire _0_qn, _1_qn, _3_qn, and_1_out, clock_1_out, or_1_out;
  wire [3:0] _0_q, divider_1_out, divider_1_rem;

  Clock clock_1 (.out(clock_1_out));
  J_K_Flip_Flop _3 (.J(1'b1), .clk(clock_1_out), .K(or_1_out), .Q(_0_q[3]), .Qn(_3_qn));  // open: preset, en, reset
  or or_1 (or_1_out, _0_q[1], _0_q[2]);
  J_K_Flip_Flop _2 (.J(_0_q[1]), .clk(clock_1_out), .K(and_1_out), .Q(_0_q[2]));  // open: Qn, preset, en, reset
  Hex_Digit_Display hex_digit_display_1 (.value(divider_1_out));  // open: dp
  Divider #(.width(4)) divider_1 (.a(_0_q), .b(4'b1010), .out(divider_1_out), .rem(divider_1_rem));  // open: upper
  J_K_Flip_Flop _1 (.J(_0_qn), .clk(clock_1_out), .K(_0_q[0]), .Q(_0_q[1]), .Qn(_1_qn));  // open: preset, en, reset
  and and_1 (and_1_out, _3_qn, _1_qn);
  Hex_Digit_Display hex_digit_display_2 (.value(divider_1_rem));  // open: dp
  J_K_Flip_Flop _0 (.J(_0_q[1]), .clk(clock_1_out), .K(and_1_out), .Q(_0_q[0]), .Qn(_0_qn));  // open: preset, en, reset
endmodule

module _2 (
);

  wire clock_1_out;
  wire [3:0] _0_q, divider_1_rem, divider_2_rem;

  Clock clock_1 (.out(clock_1_out));
  J_K_Flip_Flop _3 (.J(_0_q[0]), .clk(clock_1_out), .K(1'b1), .Q(_0_q[3]));  // open: Qn, preset, en, reset
  J_K_Flip_Flop _2 (.J(_0_q[3]), .clk(clock_1_out), .K(1'b1), .Q(_0_q[2]));  // open: Qn, preset, en, reset
  Divider #(.width(4)) divider_1 (.a(_0_q), .b(4'b1010), .rem(divider_1_rem));  // open: out, upper
  J_K_Flip_Flop _1 (.J(_0_q[2]), .clk(clock_1_out), .K(1'b1), .Q(_0_q[1]));  // open: Qn, preset, en, reset
  Divider #(.width(4)) divider_2 (
    .a({_0_q[0], _0_q[1], _0_q[2], _0_q[3]}), .b(4'b1010), .rem(divider_2_rem));  // open: out, upper
  J_K_Flip_Flop _0 (.J(_0_q[1]), .clk(clock_1_out), .K(1'b1), .Q(_0_q[0]));  // open: Qn, preset, en, reset
  Hex_Digit_Display hex_digit_display_1 (.value(divider_2_rem));  // open: dp
  Hex_Digit_Display hex_digit_display_2 (.value(divider_1_rem));  // open: dp
endmodule

module shift_right (
);

  wire _1_qn, _2_qn, _3_qn, clock_1_out;
  wire [3:0] _0_q, divider_1_out, divider_1_rem, divider_2_out, divider_2_rem;

  Clock clock_1 (.out(clock_1_out));
  J_K_Flip_Flop _3 (.J(1'b0), .clk(clock_1_out), .K(1'b1), .Q(_0_q[3]), .Qn(_3_qn));  // open: preset, en, reset
  J_K_Flip_Flop _2 (.J(_0_q[3]), .clk(clock_1_out), .K(_3_qn), .Q(_0_q[2]), .Qn(_2_qn));  // open: preset, en, reset
  Divider #(.width(4)) divider_1 (.a(_0_q), .b(4'b1010), .out(divider_1_out), .rem(divider_1_rem));  // open: upper
  J_K_Flip_Flop _1 (.J(_0_q[2]), .clk(clock_1_out), .K(_2_qn), .Q(_0_q[1]), .Qn(_1_qn));  // open: preset, en, reset
  Divider #(.width(4)) divider_2 (
    .a({_0_q[0], _0_q[1], _0_q[2], _0_q[3]}), .b(4'b1010), .out(divider_2_out), .rem(divider_2_rem));  // open: upper
  Hex_Digit_Display hex_digit_display_1 (.value(divider_1_out));  // open: dp
  J_K_Flip_Flop _0 (.J(_0_q[1]), .clk(clock_1_out), .K(_1_qn), .Q(_0_q[0]));  // open: Qn, preset, en, reset
  Hex_Digit_Display hex_digit_display_2 (.value(divider_2_rem));  // open: dp
  Hex_Digit_Display hex_digit_display_3 (.value(divider_2_out));  // open: dp
  Hex_Digit_Display hex_digit_display_4 (.value(divider_1_rem));  // open: dp
endmodule
