// Logisim project RAM.circ as structural Verilog: 1 circuit, main circuit main
module main (
  input  [1:0] \Endereço ,
  input  [3:0] Entrada,
  input  Write_Eneable,
  output [3:0] Saida
);

  wire and_1_out, and_2_out, and_3_out, and_4_out, and_5_out, and_6_out, and_7_out, and_8_out, and_9_out,
       and_10_out, and_11_out, and_12_out, and_13_out, and_14_out, and_15_out, and_16_out, and_17_out,
       and_18_out, and_19_out, and_20_out, and_21_out, and_22_out, and_23_out, and_24_out, d_ff_1_q,
       d_ff_2_q, d_ff_3_q, d_ff_4_q, d_ff_5_q, d_ff_6_q, d_ff_7_q, d_ff_8_q, d_ff_9_q, d_ff_10_q, d_ff_11_q,
       d_ff_12_q, d_ff_13_q, d_ff_14_q, d_ff_15_q, d_ff_16_q;

  and and_1 (and_1_out, ~\Endereço [1], ~\Endereço [0]);  // AND_Gate
  and and_2 (and_2_out, and_1_out, Write_Eneable);
  and and_3 (and_3_out, ~\Endereço [1], \Endereço [0]);  // AND_Gate
  and and_4 (and_4_out, and_3_out, Write_Eneable);
  and and_5 (and_5_out, \Endereço [1], ~\Endereço [0]);  // AND_Gate
  and and_6 (and_6_out, and_5_out, Write_Eneable);
  and and_7 (and_7_out, \Endereço [1], \Endereço [0]);
  and and_8 (and_8_out, and_7_out, Write_Eneable);
  D_Flip_Flop d_ff_1 (.clk(and_2_out), .D(Entrada[0]), .Q(d_ff_1_q));  // open: Qn, preset, en, reset
  D_Flip_Flop d_ff_2 (.clk(and_4_out), .D(Entrada[0]), .Q(d_ff_2_q));  // open: Qn, preset, en, reset
  D_Flip_Flop d_ff_3 (.clk(and_6_out), .D(Entrada[0]), .Q(d_ff_3_q));  // open: Qn, preset, en, reset
  D_Flip_Flop d_ff_4 (.clk(and_8_out), .D(Entrada[0]), .Q(d_ff_4_q));  // open: Qn, preset, en, reset
  and and_9 (and_9_out, d_ff_1_q, and_1_out);
  and and_10 (and_10_out, d_ff_2_q, and_3_out);
  and and_11 (and_11_out, d_ff_3_q, and_5_out);
  and and_12 (and_12_out, d_ff_4_q, and_7_out);
  or or_1 (Saida[0], and_12_out, and_11_out, and_10_out, and_9_out);
  D_Flip_Flop d_ff_5 (.clk(and_2_out), .D(Entrada[1]), .Q(d_ff_5_q));  // open: Qn, preset, en, reset
  D_Flip_Flop d_ff_6 (.clk(and_4_out), .D(Entrada[1]), .Q(d_ff_6_q));  // open: Qn, preset, en, reset
  D_Flip_Flop d_ff_7 (.clk(and_6_out), .D(Entrada[1]), .Q(d_ff_7_q));  // open: Qn, preset, en, reset
  D_Flip_Flop d_ff_8 (.clk(and_8_out), .D(Entrada[1]), .Q(d_ff_8_q));  // open: Qn, preset, en, reset
  and and_13 (and_13_out, d_ff_5_q, and_1_out);
  and and_14 (and_14_out, d_ff_6_q, and_3_out);
  and and_15 (and_15_out, d_ff_7_q, and_5_out);
  and and_16 (and_16_out, d_ff_8_q, and_7_out);
  or or_2 (Saida[1], and_16_out, and_15_out, and_14_out, and_13_out);
  D_Flip_Flop d_ff_9 (.clk(and_2_out), .D(Entrada[2]), .Q(d_ff_9_q));  // open: Qn, preset, en, reset
  D_Flip_Flop d_ff_10 (.clk(and_4_out), .D(Entrada[2]), .Q(d_ff_10_q));  // open: Qn, preset, en, reset
  D_Flip_Flop d_ff_11 (.clk(and_6_out), .D(Entrada[2]), .Q(d_ff_11_q));  // open: Qn, preset, en, reset
  D_Flip_Flop d_ff_12 (.clk(and_8_out), .D(Entrada[2]), .Q(d_ff_12_q));  // open: Qn, preset, en, reset
  and and_17 (and_17_out, d_ff_9_q, and_1_out);
  and and_18 (and_18_out, d_ff_10_q, and_3_out);
  and and_19 (and_19_out, d_ff_11_q, and_5_out);
  and and_20 (and_20_out, d_ff_12_q, and_7_out);
  or or_3 (Saida[2], and_20_out, and_19_out, and_18_out, and_17_out);
  D_Flip_Flop d_ff_13 (.clk(and_2_out), .D(Entrada[3]), .Q(d_ff_13_q));  // open: Qn, preset, en, reset
  and and_21 (and_21_out, d_ff_13_q, and_1_out);
  D_Flip_Flop d_ff_14 (.clk(and_4_out), .D(Entrada[3]), .Q(d_ff_14_q));  // open: Qn, preset, en, reset
  and and_22 (and_22_out, d_ff_14_q, and_3_out);
  D_Flip_Flop d_ff_15 (.clk(and_6_out), .D(Entrada[3]), .Q(d_ff_15_q));  // open: Qn, preset, en, reset
  and and_23 (and_23_out, d_ff_15_q, and_5_out);
  D_Flip_Flop d_ff_16 (.clk(and_8_out), .D(Entrada[3]), .Q(d_ff_16_q));  // open: Qn, preset, en, reset
  and and_24 (and_24_out, d_ff_16_q, and_7_out);
  or or_4 (Saida[3], and_24_out, and_23_out, and_22_out, and_21_out);
endmodule
