// Logisim project Relogio.circ as structural Verilog: 5 circuits, main circuit relogio
module relogio (
);

  wire clock_1_out, contador_05_1_q, contador_05_2_q, contador_09_1_q, contador_09_2_q, demux_1_a, demux_1_b,
       demux_1_c, demux_1_d, demux_1_e, demux_1_f, demux_1_g, demux_2_a, demux_2_b, demux_2_c, demux_2_d,
       demux_2_e, demux_2_f, demux_2_g, demux_3_a, demux_3_b, demux_3_c, demux_3_d, demux_3_e, demux_3_f,
       demux_3_g, demux_4_a, demux_4_b, demux_4_c, demux_4_d, demux_4_e, demux_4_f, demux_4_g, demux_5_a,
       demux_5_b, demux_5_c, demux_5_d, demux_5_e, demux_5_f, demux_5_g, demux_6_a, demux_6_b, demux_6_c,
       demux_6_d, demux_6_e, demux_6_f, demux_6_g;
  wire [3:0] dH, dM, dS, uH, uM, uS;

  _7_Segment_Display u_7_segment_display_1 (
    .g(demux_1_g), .f(demux_1_f), .a(demux_1_a), .b(demux_1_b), .e(demux_1_e), .d(demux_1_d), .c(demux_1_c));  // open: dp
  Contador_Horas contador_horas_1 (.Clock(contador_05_1_q), .Dezena(dH), .Unidade(uH));  // open: Set
  _7_Segment_Display u_7_segment_display_2 (
    .g(demux_2_g), .f(demux_2_f), .a(demux_2_a), .b(demux_2_b), .e(demux_2_e), .d(demux_2_d), .c(demux_2_c));  // open: dp
  demux demux_1 (
    .in_1(dH), .a(demux_1_a), .b(demux_1_b), .c(demux_1_c), .d(demux_1_d), .e(demux_1_e), .f(demux_1_f),
    .g(demux_1_g));
  demux demux_2 (
    .in_1(uH), .a(demux_2_a), .b(demux_2_b), .c(demux_2_c), .d(demux_2_d), .e(demux_2_e), .f(demux_2_f),
    .g(demux_2_g));
  Contador_05 contador_05_1 (.Clock(contador_09_1_q), .out_3(dM), .Q(contador_05_1_q));
  _7_Segment_Display u_7_segment_display_3 (
    .g(demux_3_g), .f(demux_3_f), .a(demux_3_a), .b(demux_3_b), .e(demux_3_e), .d(demux_3_d), .c(demux_3_c));  // open: dp
  demux demux_3 (
    .in_1(dM), .a(demux_3_a), .b(demux_3_b), .c(demux_3_c), .d(demux_3_d), .e(demux_3_e), .f(demux_3_f),
    .g(demux_3_g));
  Contador_09 contador_09_1 (.Clock(contador_05_2_q), .out_3(uM), .Q(contador_09_1_q));
  _7_Segment_Display u_7_segment_display_4 (
    .g(demux_4_g), .f(demux_4_f), .a(demux_4_a), .b(demux_4_b), .e(demux_4_e), .d(demux_4_d), .c(demux_4_c));  // open: dp
  demux demux_4 (
    .in_1(uM), .a(demux_4_a), .b(demux_4_b), .c(demux_4_c), .d(demux_4_d), .e(demux_4_e), .f(demux_4_f),
    .g(demux_4_g));
  Contador_05 contador_05_2 (.Clock(contador_09_2_q), .out_3(dS), .Q(contador_05_2_q));
  _7_Segment_Display u_7_segment_display_5 (
    .g(demux_5_g), .f(demux_5_f), .a(demux_5_a), .b(demux_5_b), .e(demux_5_e), .d(demux_5_d), .c(demux_5_c));  // open: dp
  demux demux_5 (
    .in_1(dS), .a(demux_5_a), .b(demux_5_b), .c(demux_5_c), .d(demux_5_d), .e(demux_5_e), .f(demux_5_f),
    .g(demux_5_g));
  _7_Segment_Display u_7_segment_display_6 (
    .g(demux_6_g), .f(demux_6_f), .a(demux_6_a), .b(demux_6_b), .e(demux_6_e), .d(demux_6_d), .c(demux_6_c));  // open: dp
  demux demux_6 (
    .in_1(uS), .a(demux_6_a), .b(demux_6_b), .c(demux_6_c), .d(demux_6_d), .e(demux_6_e), .f(demux_6_f),
    .g(demux_6_g));
  Clock clock_1 (.out(clock_1_out));
  Contador_09 contador_09_2 (.Clock(clock_1_out), .out_3(uS), .Q(contador_09_2_q));
endmodule

module demux (
  input  [3:0] in_1,
  output a,
  output b,
  output c,
  output d,
  output e,
  output f,
  output g
);

  wire and_1_out, and_2_out, and_3_out, and_4_out, and_5_out, and_6_out, and_7_out, and_8_out, and_9_out,
       and_10_out, and_11_out, and_12_out, and_13_out, and_14_out, and_15_out, and_16_out, not_1_out,
       not_2_out, not_3_out, not_4_out, not_5_out, not_6_out, not_7_out, not_8_out, not_9_out, not_10_out,
       not_11_out, not_12_out, not_13_out, not_14_out, not_15_out, not_16_out, not_17_out, not_18_out,
       not_19_out, not_20_out, not_21_out;

  not not_1 (not_1_out, in_1[2]);
  not not_2 (not_2_out, in_1[0]);
  not not_3 (not_3_out, in_1[1]);
  not not_4 (not_4_out, in_1[0]);
  not not_5 (not_5_out, in_1[1]);
  not not_6 (not_6_out, in_1[2]);
  not not_7 (not_7_out, in_1[0]);
  not not_8 (not_8_out, in_1[2]);
  not not_9 (not_9_out, in_1[0]);
  not not_10 (not_10_out, in_1[1]);
  not not_11 (not_11_out, in_1[2]);
  not not_12 (not_12_out, in_1[0]);
  not not_13 (not_13_out, in_1[0]);
  not not_14 (not_14_out, in_1[1]);
  not not_15 (not_15_out, in_1[0]);
  not not_16 (not_16_out, in_1[1]);
  not not_17 (not_17_out, in_1[0]);
  not not_18 (not_18_out, in_1[2]);
  not not_19 (not_19_out, in_1[1]);
  not not_20 (not_20_out, in_1[0]);
  and and_1 (and_1_out, not_1_out, not_2_out);
  and and_2 (and_2_out, in_1[2], in_1[0]);
  not not_21 (not_21_out, in_1[2]);
  and and_3 (and_3_out, not_3_out, not_4_out);
  and and_4 (and_4_out, in_1[1], in_1[0]);
  or or_1 (c, not_5_out, in_1[0], in_1[2]);
  and and_5 (and_5_out, not_6_out, not_7_out);
  and and_6 (and_6_out, not_8_out, in_1[1]);
  and and_7 (and_7_out, in_1[1], not_9_out);
  and and_8 (and_8_out, in_1[2], not_10_out, in_1[0]);
  and and_9 (and_9_out, not_11_out, not_12_out);
  and and_10 (and_10_out, in_1[1], not_13_out);
  and and_11 (and_11_out, not_14_out, not_15_out);
  and and_12 (and_12_out, in_1[2], not_16_out);
  and and_13 (and_13_out, in_1[2], not_17_out);
  and and_14 (and_14_out, not_18_out, in_1[1]);
  and and_15 (and_15_out, in_1[2], not_19_out);
  and and_16 (and_16_out, in_1[2], not_20_out);
  or or_2 (a, and_1_out, in_1[1], and_2_out, in_1[3]);
  or or_3 (b, not_21_out, and_3_out, and_4_out);
  or or_4 (d, and_5_out, and_6_out, and_7_out, and_8_out, in_1[3]);
  or or_5 (e, and_9_out, and_10_out);
  or or_6 (f, and_11_out, and_12_out, and_13_out, in_1[3]);
  or or_7 (g, and_14_out, and_15_out, and_16_out, in_1[3]);
endmodule

module Contador_09 (
  input  Clock,
  output Q,
  output [3:0] out_3
);

  and and_1 (Q, out_3[3], ~out_3[2], out_3[1], ~out_3[0]);  // AND_Gate
  T_Flip_Flop #(.trigger("falling")) t_ff_1 (.clk(Clock), .T(1'b1), .Q(out_3[0]), .reset(Q));  // open: Qn, preset, en
  T_Flip_Flop #(.trigger("falling")) t_ff_2 (
    .clk(out_3[0]), .T(1'b1), .Q(out_3[1]), .reset(Q));  // open: Qn, preset, en
  T_Flip_Flop #(.trigger("falling")) t_ff_3 (
    .clk(out_3[1]), .T(1'b1), .Q(out_3[2]), .reset(Q));  // open: Qn, preset, en
  T_Flip_Flop #(.trigger("falling")) t_ff_4 (
    .clk(out_3[2]), .T(1'b1), .Q(out_3[3]), .reset(Q));  // open: Qn, preset, en
endmodule

module Contador_05 (
  input  Clock,
  output Q,
  output [3:0] out_3
);

  T_Flip_Flop #(.trigger("falling")) t_ff_1 (.clk(Clock), .T(1'b1), .Q(out_3[0]), .reset(Q));  // open: Qn, preset, en
  // Probe on out_3
  T_Flip_Flop #(.trigger("falling")) t_ff_2 (
    .clk(out_3[0]), .T(1'b1), .Q(out_3[1]), .reset(Q));  // open: Qn, preset, en
  and and_1 (Q, ~out_3[3], out_3[2], out_3[1], ~out_3[0]);  // AND_Gate
  T_Flip_Flop #(.trigger("falling")) t_ff_3 (
    .clk(out_3[1]), .T(1'b1), .Q(out_3[2]), .reset(Q));  // open: Qn, preset, en
  T_Flip_Flop #(.trigger("falling")) t_ff_4 (
    .clk(out_3[2]), .T(1'b1), .Q(out_3[3]), .reset(Q));  // open: Qn, preset, en
endmodule

module Contador_Horas (
  input  Clock,
  output [3:0] Unidade,
  output [3:0] Dezena,
  output Set
);

  wire and_1_out, and_2_out, and_4_out, and_5_out, or_1_out, or_2_out;

  and and_1 (and_1_out, ~Unidade[3], Unidade[2], ~Unidade[1], ~Unidade[0]);  // AND_Gate
  T_Flip_Flop #(.trigger("falling")) t_ff_1 (
    .clk(Clock), .T(1'b1), .Q(Unidade[0]), .reset(or_1_out));  // open: Qn, preset, en
  T_Flip_Flop #(.trigger("falling")) t_ff_2 (
    .clk(Unidade[0]), .T(1'b1), .Q(Unidade[1]), .reset(or_1_out));  // open: Qn, preset, en
  and and_2 (and_2_out, Unidade[3], ~Unidade[2], Unidade[1], ~Unidade[0]);  // AND_Gate
  // Probe on Unidade
  T_Flip_Flop #(.trigger("falling")) t_ff_3 (
    .clk(Unidade[1]), .T(1'b1), .Q(Unidade[2]), .reset(or_1_out));  // open: Qn, preset, en
  or or_1 (or_1_out, Set, and_2_out);
  and and_3 (Set, and_1_out, and_5_out);
  T_Flip_Flop #(.trigger("falling")) t_ff_4 (
    .clk(Unidade[2]), .T(1'b1), .Q(Unidade[3]), .reset(or_1_out));  // open: Qn, preset, en
  T_Flip_Flop #(.trigger("falling")) t_ff_5 (
    .clk(and_2_out), .T(1'b1), .Q(Dezena[0]), .reset(or_2_out));  // open: Qn, preset, en
  // Probe on Dezena
  T_Flip_Flop #(.trigger("falling")) t_ff_6 (
    .clk(Dezena[0]), .T(1'b1), .Q(Dezena[1]), .reset(or_2_out));  // open: Qn, preset, en
  T_Flip_Flop #(.trigger("falling")) t_ff_7 (
    .clk(Dezena[1]), .T(1'b1), .Q(Dezena[2]), .reset(or_2_out));  // open: Qn, preset, en
  and and_4 (and_4_out, Dezena[3], ~Dezena[2], Dezena[1], ~Dezena[0]);  // AND_Gate
  and and_5 (and_5_out, ~Dezena[3], ~Dezena[2], Dezena[1], ~Dezena[0]);  // AND_Gate
  T_Flip_Flop #(.trigger("falling")) t_ff_8 (
    .clk(Dezena[2]), .T(1'b1), .Q(Dezena[3]), .reset(or_2_out));  // open: Qn, preset, en
  or or_2 (or_2_out, and_4_out, Set);
endmodule
