// Logisim project Somador Look Ahead 8 bits.circ as structural Verilog
module _1bit (
  input  Op,
  output [7:0] out_2
);


  assign out_2 = {8{Op}};
endmodule

module somador_1bit (
  input  A,
  input  B,
  input  Cin,
  output Cout,
  output S
);

  wire and_1_out, and_2_out, and_3_out, xor_1_out;

  and and_1 (and_1_out, A, B);
  and and_2 (and_2_out, A, Cin);
  and and_3 (and_3_out, B, Cin);
  xor xor_1 (xor_1_out, A, B);
  xor xor_2 (S, xor_1_out, Cin);
  or or_1 (Cout, and_1_out, and_2_out, and_3_out);
endmodule

module soma_e_subtrai_8bits_lookahead (
  input  Op,
  input  [7:0] B,
  input  [7:0] A,
  output [7:0] S
);

  wire and_1_out, and_2_out, and_3_out, and_4_out, and_5_out, and_6_out, and_7_out, and_8_out, and_9_out,
       and_10_out, and_11_out, and_12_out, and_13_out, and_14_out, and_15_out, and_16_out, and_17_out,
       and_18_out, and_19_out, and_20_out, and_21_out, and_22_out, and_23_out, and_24_out, and_25_out,
       and_26_out, and_27_out, and_28_out, and_29_out, and_30_out, and_31_out, and_32_out, and_33_out,
       and_34_out, and_35_out, and_36_out, G0___P0_g__a_b, G0___P0_p__a_b, G1___P1_g__a_b, G1___P1_p__a_b,
       G2___P2_g__a_b, G2___P2_p__a_b, G3___P3_g__a_b, G3___P3_p__a_b, G4___P4_g__a_b, G4___P4_p__a_b,
       G5___P5_g__a_b, G5___P5_p__a_b, G6___P6_g__a_b, G6___P6_p__a_b, G7___P7_g__a_b, G7___P7_p__a_b,
       or_1_out, or_2_out, or_3_out, or_4_out, or_5_out, or_6_out, or_7_out, or_8_out;
  wire [7:0] n1bit_1_out_2, xor_1_out;

  _1bit u_1bit_1 (.Op(Op), .out_2(n1bit_1_out_2));
  // Probe on B
  // Probe on S
  // Probe on S
  assign xor_1_out = n1bit_1_out_2 ^ B;  // XOR_Gate xor_1, 8 bits wide
  // Probe on A
  GP G0___P0 (.A(A[0]), .B(xor_1_out[0]), .G__A_B(G0___P0_g__a_b), .P__A_B(G0___P0_p__a_b));
  GP G1___P1 (.A(A[1]), .B(xor_1_out[1]), .G__A_B(G1___P1_g__a_b), .P__A_B(G1___P1_p__a_b));
  GP G2___P2 (.A(A[2]), .B(xor_1_out[2]), .G__A_B(G2___P2_g__a_b), .P__A_B(G2___P2_p__a_b));
  GP G3___P3 (.A(A[3]), .B(xor_1_out[3]), .G__A_B(G3___P3_g__a_b), .P__A_B(G3___P3_p__a_b));
  GP G4___P4 (.A(A[4]), .B(xor_1_out[4]), .G__A_B(G4___P4_g__a_b), .P__A_B(G4___P4_p__a_b));
  GP G5___P5 (.A(A[5]), .B(xor_1_out[5]), .G__A_B(G5___P5_g__a_b), .P__A_B(G5___P5_p__a_b));
  GP G6___P6 (.A(A[6]), .B(xor_1_out[6]), .G__A_B(G6___P6_g__a_b), .P__A_B(G6___P6_p__a_b));
  GP G7___P7 (.A(xor_1_out[7]), .B(A[7]), .G__A_B(G7___P7_g__a_b), .P__A_B(G7___P7_p__a_b));
  and and_1 (and_1_out, G7___P7_p__a_b, G6___P6_g__a_b);
  or or_1 (or_1_out, G7___P7_g__a_b, and_1_out, and_3_out, and_2_out, and_4_out, and_5_out, and_6_out, and_7_out, and_8_out);
  LED Overflow (.in(or_1_out));
  and and_2 (and_2_out, G7___P7_p__a_b, G6___P6_p__a_b, G5___P5_p__a_b, G4___P4_g__a_b);
  and and_3 (and_3_out, G7___P7_p__a_b, G6___P6_p__a_b, G5___P5_g__a_b);
  and and_4 (and_4_out, G7___P7_p__a_b, G6___P6_p__a_b, G5___P5_p__a_b, G4___P4_p__a_b, G3___P3_g__a_b);
  and and_5 (and_5_out, G7___P7_p__a_b, G6___P6_p__a_b, G5___P5_p__a_b, G4___P4_p__a_b, G3___P3_p__a_b, G2___P2_g__a_b);
  and and_6 (and_6_out, G7___P7_p__a_b, G6___P6_p__a_b, G5___P5_p__a_b, G4___P4_p__a_b, G3___P3_p__a_b, G2___P2_p__a_b, G1___P1_g__a_b);
  and and_7 (and_7_out, G7___P7_p__a_b, G6___P6_p__a_b, G5___P5_p__a_b, G4___P4_p__a_b, G3___P3_p__a_b, G2___P2_p__a_b, G1___P1_p__a_b, G0___P0_g__a_b);
  and and_8 (and_8_out, G7___P7_p__a_b, G6___P6_p__a_b, G5___P5_p__a_b, G4___P4_p__a_b, G3___P3_p__a_b, G2___P2_p__a_b, G1___P1_p__a_b, G0___P0_p__a_b, Op);
  somador_lookahead somador_lookahead_1 (.S(S[7]), .A(A[7]), .B(xor_1_out[7]), .Cin(or_2_out));
  and and_9 (and_9_out, G6___P6_p__a_b, G5___P5_g__a_b);
  and and_10 (and_10_out, G6___P6_p__a_b, G5___P5_p__a_b, G4___P4_g__a_b);
  or or_2 (or_2_out, G6___P6_g__a_b, and_9_out, and_10_out, and_11_out, and_12_out, and_13_out, and_14_out, and_15_out);
  and and_11 (and_11_out, G6___P6_p__a_b, G5___P5_p__a_b, G4___P4_p__a_b, G3___P3_g__a_b);
  and and_12 (and_12_out, G6___P6_p__a_b, G5___P5_p__a_b, G4___P4_p__a_b, G3___P3_p__a_b, G2___P2_g__a_b);
  and and_13 (and_13_out, G6___P6_p__a_b, G5___P5_p__a_b, G4___P4_p__a_b, G3___P3_p__a_b, G2___P2_p__a_b, G1___P1_g__a_b);
  and and_14 (and_14_out, G6___P6_p__a_b, G5___P5_p__a_b, G4___P4_p__a_b, G3___P3_p__a_b, G2___P2_p__a_b, G1___P1_p__a_b, G0___P0_g__a_b);
  and and_15 (and_15_out, G6___P6_p__a_b, G5___P5_p__a_b, G4___P4_p__a_b, G3___P3_p__a_b, G2___P2_p__a_b, G1___P1_p__a_b, G0___P0_p__a_b, Op);
  somador_lookahead somador_lookahead_2 (.S(S[6]), .A(A[6]), .B(xor_1_out[6]), .Cin(or_3_out));
  and and_16 (and_16_out, G5___P5_p__a_b, G4___P4_g__a_b);
  and and_17 (and_17_out, G5___P5_p__a_b, G4___P4_p__a_b, G3___P3_g__a_b);
  or or_3 (or_3_out, G5___P5_g__a_b, and_16_out, and_17_out, and_18_out, and_19_out, and_20_out, and_21_out);
  and and_18 (and_18_out, G5___P5_p__a_b, G4___P4_p__a_b, G3___P3_p__a_b, G2___P2_g__a_b);
  and and_19 (and_19_out, G5___P5_p__a_b, G4___P4_p__a_b, G3___P3_p__a_b, G2___P2_p__a_b, G1___P1_g__a_b);
  and and_20 (and_20_out, G5___P5_p__a_b, G4___P4_p__a_b, G3___P3_p__a_b, G2___P2_p__a_b, G1___P1_p__a_b, G0___P0_g__a_b);
  and and_21 (and_21_out, G5___P5_p__a_b, G4___P4_p__a_b, G3___P3_p__a_b, G2___P2_p__a_b, G1___P1_p__a_b, G0___P0_p__a_b, Op);
  and and_22 (and_22_out, G4___P4_p__a_b, G3___P3_g__a_b);
  or or_4 (or_4_out, G4___P4_g__a_b, and_22_out, and_23_out, and_24_out, and_26_out, and_25_out);
  somador_lookahead somador_lookahead_3 (.S(S[5]), .A(A[5]), .B(xor_1_out[5]), .Cin(or_4_out));
  and and_23 (and_23_out, G4___P4_p__a_b, G3___P3_p__a_b, G2___P2_g__a_b);
  and and_24 (and_24_out, G4___P4_p__a_b, G3___P3_p__a_b, G2___P2_p__a_b, G1___P1_g__a_b);
  and and_25 (and_25_out, G4___P4_p__a_b, G3___P3_p__a_b, G2___P2_p__a_b, G1___P1_p__a_b, G0___P0_p__a_b, Op);
  and and_26 (and_26_out, G4___P4_p__a_b, G3___P3_p__a_b, G2___P2_p__a_b, G1___P1_p__a_b, G0___P0_g__a_b);
  somador_lookahead somador_lookahead_4 (.S(S[4]), .A(A[4]), .B(xor_1_out[4]), .Cin(or_5_out));
  and and_27 (and_27_out, G3___P3_p__a_b, G2___P2_g__a_b);
  and and_28 (and_28_out, G3___P3_p__a_b, G2___P2_p__a_b, G1___P1_g__a_b);
  or or_5 (or_5_out, G3___P3_g__a_b, and_27_out, and_28_out, and_29_out, and_30_out);
  and and_29 (and_29_out, G3___P3_p__a_b, G2___P2_p__a_b, G1___P1_p__a_b, G0___P0_g__a_b);
  and and_30 (and_30_out, G3___P3_p__a_b, G2___P2_p__a_b, G1___P1_p__a_b, G0___P0_p__a_b, Op);
  and and_31 (and_31_out, G2___P2_p__a_b, G1___P1_g__a_b);
  or or_6 (or_6_out, G2___P2_g__a_b, and_31_out, and_32_out, and_33_out);
  somador_lookahead somador_lookahead_5 (.S(S[3]), .A(A[3]), .B(xor_1_out[3]), .Cin(or_6_out));
  and and_32 (and_32_out, G2___P2_p__a_b, G1___P1_p__a_b, G0___P0_g__a_b);
  and and_33 (and_33_out, G2___P2_p__a_b, G1___P1_p__a_b, G0___P0_p__a_b, Op);
  somador_lookahead somador_lookahead_6 (.S(S[2]), .A(A[2]), .B(xor_1_out[2]), .Cin(or_7_out));
  and and_34 (and_34_out, G1___P1_p__a_b, G0___P0_g__a_b);
  and and_35 (and_35_out, G1___P1_p__a_b, G0___P0_p__a_b, Op);
  or or_7 (or_7_out, G1___P1_g__a_b, and_34_out, and_35_out);
  and and_36 (and_36_out, G0___P0_p__a_b, Op);
  or or_8 (or_8_out, G0___P0_g__a_b, and_36_out);
  somador_lookahead somador_lookahead_7 (.S(S[1]), .A(A[1]), .B(xor_1_out[1]), .Cin(or_8_out));
  somador_lookahead somador_lookahead_8 (.S(S[0]), .A(A[0]), .B(xor_1_out[0]), .Cin(Op));

  // Notes on the sheet:
  //   Complemento de 2
endmodule

module GP (
  input  A,
  input  B,
  output G__A_B,
  output P__A_B
);

  and and_1 (G__A_B, A, B);
  or or_1 (P__A_B, A, B);
endmodule

module somador_lookahead (
  input  A,
  input  B,
  input  Cin,
  output S
);

  wire xor_1_out;

  xor xor_1 (xor_1_out, A, B);
  xor xor_2 (S, xor_1_out, Cin);
endmodule
