// Logisim project Somador Ripple Carry 32 bits.circ as structural Verilog: 7 circuits, main circuit main
module main (
  input  A,
  input  B,
  input  Cin,
  output Cout,
  output S
);

  wire and_1_out, and_2_out, and_3_out, xor_1_out;

  and and_1 (and_1_out, A, B);
  and and_2 (and_2_out, A, Cin);
  and and_3 (and_3_out, B, Cin);
  xor xor_1 (xor_1_out, A, B);
  xor xor_2 (S, xor_1_out, Cin);
  or or_1 (Cout, and_1_out, and_2_out, and_3_out);
endmodule

module somador_8bits (
  input  [7:0] A,
  input  [7:0] B,
  input  Cin,
  output Cout,
  output [7:0] S
);

  wire main_1_cout, main_3_cout, main_4_cout, main_5_cout, main_6_cout, main_7_cout, main_8_cout;

  main main_1 (.Cout(main_1_cout), .S(S[6]), .A(B[6]), .B(A[6]), .Cin(main_3_cout));
  main main_2 (.Cout(Cout), .S(S[7]), .A(B[7]), .B(A[7]), .Cin(main_1_cout));
  main main_3 (.Cout(main_3_cout), .S(S[5]), .A(B[5]), .B(A[5]), .Cin(main_4_cout));
  main main_4 (.Cout(main_4_cout), .S(S[4]), .A(B[4]), .B(A[4]), .Cin(main_5_cout));
  main main_5 (.Cout(main_5_cout), .S(S[3]), .A(B[3]), .B(A[3]), .Cin(main_6_cout));
  main main_6 (.Cout(main_6_cout), .S(S[2]), .A(B[2]), .B(A[2]), .Cin(main_7_cout));
  main main_7 (.Cout(main_7_cout), .S(S[1]), .A(B[1]), .B(A[1]), .Cin(main_8_cout));
  main main_8 (.Cout(main_8_cout), .S(S[0]), .A(B[0]), .B(A[0]), .Cin(Cin));
endmodule

module somador_32bits (
  input  [31:0] A,
  input  [31:0] B,
  input  Cin,
  output Cout,
  output [31:0] S
);

  wire somador_8bits_1_cout, somador_8bits_3_cout, somador_8bits_4_cout;

  somador_8bits somador_8bits_1 (
    .A(A[23:16]), .B(B[23:16]), .Cout(somador_8bits_1_cout), .S(S[23:16]), .Cin(somador_8bits_3_cout));
  somador_8bits somador_8bits_2 (.A(A[31:24]), .B(B[31:24]), .Cout(Cout), .S(S[31:24]), .Cin(somador_8bits_1_cout));
  somador_8bits somador_8bits_3 (
    .A(A[15:8]), .B(B[15:8]), .Cout(somador_8bits_3_cout), .S(S[15:8]), .Cin(somador_8bits_4_cout));
  somador_8bits somador_8bits_4 (.A(A[7:0]), .B(B[7:0]), .Cout(somador_8bits_4_cout), .S(S[7:0]), .Cin(Cin));
endmodule

module sub_1b (
  input  A,
  input  B,
  input  Cin,
  output Cout,
  output S
);

  wire and_1_out, and_2_out, and_3_out, xor_1_out;

  and and_1 (and_1_out, ~A, B);  // AND_Gate
  and and_2 (and_2_out, ~A, Cin);  // AND_Gate
  and and_3 (and_3_out, B, Cin);
  xor xor_1 (xor_1_out, A, B);
  xor xor_2 (S, xor_1_out, Cin);
  or or_1 (Cout, and_1_out, and_2_out, and_3_out);
endmodule

module sub_8bits (
  input  [7:0] A,
  input  [7:0] B,
  input  Cin,
  output Cout,
  output [7:0] S
);

  wire sub_1b_2_cout, sub_1b_3_cout, sub_1b_4_cout, sub_1b_5_cout, sub_1b_6_cout, sub_1b_7_cout,
       sub_1b_8_cout;

  sub_1b sub_1b_1 (.Cout(Cout), .S(S[7]), .A(A[7]), .B(B[7]), .Cin(sub_1b_3_cout));
  sub_1b sub_1b_2 (.Cout(sub_1b_2_cout), .S(S[5]), .A(A[5]), .B(B[5]), .Cin(sub_1b_4_cout));
  sub_1b sub_1b_3 (.Cout(sub_1b_3_cout), .S(S[6]), .A(A[6]), .B(B[6]), .Cin(sub_1b_2_cout));
  sub_1b sub_1b_4 (.Cout(sub_1b_4_cout), .S(S[4]), .A(A[4]), .B(B[4]), .Cin(sub_1b_5_cout));
  sub_1b sub_1b_5 (.Cout(sub_1b_5_cout), .S(S[3]), .A(A[3]), .B(B[3]), .Cin(sub_1b_7_cout));
  sub_1b sub_1b_6 (.Cout(sub_1b_6_cout), .S(S[1]), .A(A[1]), .B(B[1]), .Cin(sub_1b_8_cout));
  sub_1b sub_1b_7 (.Cout(sub_1b_7_cout), .S(S[2]), .A(A[2]), .B(B[2]), .Cin(sub_1b_6_cout));
  sub_1b sub_1b_8 (.Cout(sub_1b_8_cout), .S(S[0]), .A(A[0]), .B(B[0]), .Cin(Cin));
endmodule

module soma_e_subtrai_8bits (
  input  [7:0] A,
  input  Op,
  input  [7:0] B,
  output Cout,
  output [7:0] S
);

  wire main_2_cout, main_3_cout, main_4_cout, main_5_cout, main_6_cout, main_7_cout, main_8_cout;
  wire [7:0] n1bit_1_out_2, xor_1_out;

  _1bit u_1bit_1 (.Op(Op), .out_2(n1bit_1_out_2));
  assign xor_1_out = n1bit_1_out_2 ^ B;  // XOR_Gate xor_1, 8 bits wide
  main main_1 (.Cout(Cout), .S(S[7]), .A(xor_1_out[7]), .B(A[7]), .Cin(main_2_cout));
  main main_2 (.Cout(main_2_cout), .S(S[6]), .A(xor_1_out[6]), .B(A[6]), .Cin(main_3_cout));
  main main_3 (.Cout(main_3_cout), .S(S[5]), .A(xor_1_out[5]), .B(A[5]), .Cin(main_4_cout));
  main main_4 (.Cout(main_4_cout), .S(S[4]), .A(xor_1_out[4]), .B(A[4]), .Cin(main_6_cout));
  main main_5 (.Cout(main_5_cout), .S(S[2]), .A(xor_1_out[2]), .B(A[2]), .Cin(main_8_cout));
  main main_6 (.Cout(main_6_cout), .S(S[3]), .A(xor_1_out[3]), .B(A[3]), .Cin(main_5_cout));
  main main_7 (.Cout(main_7_cout), .S(S[0]), .A(xor_1_out[0]), .B(A[0]), .Cin(Op));
  main main_8 (.Cout(main_8_cout), .S(S[1]), .A(xor_1_out[1]), .B(A[1]), .Cin(main_7_cout));

  // Notes on the sheet:
  //   Complemento de 2
endmodule

module _1bit (
  input  Op,
  output [7:0] out_2
);


  assign out_2 = {8{Op}};
endmodule
