// Logisim project Trabalho Final.circ as structural Verilog: 3 circuits, main circuit main
module main (
  input  [10:0] in_1
);

  wire button_1_out, clock_1_out, or_1_out;
  wire [2:0] contador_0_7_1_out_2;
  wire [7:0] \acumulador_1_saída , main_2_p4;
  wire [10:0] main_1_p4;

  Clock clock_1 (.out(clock_1_out));
  Button button_1 (.out(button_1_out));
  or or_1 (or_1_out, button_1_out, clock_1_out);
  Contador_0_7 contador_0_7_1 (.E(clock_1_out), .out_2(contador_0_7_1_out_2));
  // RAM_8x11_main main_1: pin names not known; wires that end beside it: button_1_out, contador_0_7_1_out_2, in_1, main_1_p4
  Acumulador acumulador_1 (.Entrada(main_2_p4), .WE(or_1_out), .\Saída (\acumulador_1_saída ));
  // Probe on \acumulador_1_saída 
  // ULA_main main_2: pin names not known; wires that end beside it: \acumulador_1_saída , main_1_p4[7:0], main_1_p4[10:8], main_2_p4

  // Notes on the sheet:
  //   000 - AND
  //   001 - OR
  //   010 - XOR
  //   011 - Soma
  //   100 - Subtrai
  //   101 - Multiplica
  //   110 - Divide
  //   111 - Resto da Divisão
endmodule

module Contador_0_7 (
  input  E,
  output [2:0] out_2
);

  T_Flip_Flop #(.trigger("falling")) t_ff_1 (.clk(E), .T(1'b1), .Q(out_2[0]));  // open: Qn, preset, reset, en
  T_Flip_Flop #(.trigger("falling")) t_ff_2 (.clk(out_2[0]), .T(1'b1), .Q(out_2[1]));  // open: Qn, preset, reset, en
  T_Flip_Flop #(.trigger("falling")) t_ff_3 (.clk(out_2[1]), .T(1'b1), .Q(out_2[2]));  // open: Qn, preset, reset, en
endmodule

module Acumulador (
  input  [7:0] Entrada,
  input  WE,
  output [7:0] \Saída 
);

  D_Flip_Flop #(.trigger("falling")) d_ff_1 (.clk(WE), .D(Entrada[0]), .Q(\Saída [0]));  // open: Qn, preset, en, reset
  D_Flip_Flop #(.trigger("falling")) d_ff_2 (.clk(WE), .D(Entrada[1]), .Q(\Saída [1]));  // open: Qn, preset, en, reset
  D_Flip_Flop #(.trigger("falling")) d_ff_3 (.clk(WE), .D(Entrada[2]), .Q(\Saída [2]));  // open: Qn, preset, en, reset
  D_Flip_Flop #(.trigger("falling")) d_ff_4 (.clk(WE), .D(Entrada[3]), .Q(\Saída [3]));  // open: Qn, preset, en, reset
  D_Flip_Flop #(.trigger("falling")) d_ff_5 (.clk(WE), .D(Entrada[4]), .Q(\Saída [4]));  // open: Qn, preset, en, reset
  D_Flip_Flop #(.trigger("falling")) d_ff_6 (.clk(WE), .D(Entrada[5]), .Q(\Saída [5]));  // open: Qn, preset, en, reset
  D_Flip_Flop #(.trigger("falling")) d_ff_7 (.clk(WE), .D(Entrada[6]), .Q(\Saída [6]));  // open: Qn, preset, en, reset
  D_Flip_Flop #(.trigger("falling")) d_ff_8 (.clk(WE), .D(Entrada[7]), .Q(\Saída [7]));  // open: Qn, preset, en, reset
endmodule
