// Logisim project mux.circ as structural Verilog
module _1bit (
  input  Op,
  output [7:0] out_2
);


  assign out_2 = {8{Op}};
endmodule

module somador_completo_mux (
  input  [7:0] A,
  input  Op,
  input  [7:0] B,
  output Cout,
  output [7:0] S
);

  wire somador_1bit_2_cout, somador_1bit_3_cout, somador_1bit_4_cout, somador_1bit_5_cout,
       somador_1bit_6_cout, somador_1bit_7_cout, somador_1bit_8_cout;
  wire [7:0] n1bit_1_out_2, xor_1_out;

  _1bit u_1bit_1 (.Op(Op), .out_2(n1bit_1_out_2));
  assign xor_1_out = n1bit_1_out_2 ^ B;  // XOR_Gate xor_1, 8 bits wide
  somador_1bit somador_1bit_1 (.Cout(Cout), .S(S[7]), .A(xor_1_out[7]), .B(A[7]), .Cin(somador_1bit_3_cout));
  somador_1bit somador_1bit_2 (
    .Cout(somador_1bit_2_cout), .S(S[5]), .A(xor_1_out[5]), .B(A[5]), .Cin(somador_1bit_5_cout));
  somador_1bit somador_1bit_3 (
    .Cout(somador_1bit_3_cout), .S(S[6]), .A(xor_1_out[6]), .B(A[6]), .Cin(somador_1bit_2_cout));
  somador_1bit somador_1bit_4 (
    .Cout(somador_1bit_4_cout), .S(S[3]), .A(xor_1_out[3]), .B(A[3]), .Cin(somador_1bit_7_cout));
  somador_1bit somador_1bit_5 (
    .Cout(somador_1bit_5_cout), .S(S[4]), .A(xor_1_out[4]), .B(A[4]), .Cin(somador_1bit_4_cout));
  somador_1bit somador_1bit_6 (
    .Cout(somador_1bit_6_cout), .S(S[1]), .A(xor_1_out[1]), .B(A[1]), .Cin(somador_1bit_8_cout));
  somador_1bit somador_1bit_7 (
    .Cout(somador_1bit_7_cout), .S(S[2]), .A(xor_1_out[2]), .B(A[2]), .Cin(somador_1bit_6_cout));
  somador_1bit somador_1bit_8 (.Cout(somador_1bit_8_cout), .S(S[0]), .A(xor_1_out[0]), .B(A[0]), .Cin(Op));

  // Notes on the sheet:
  //   Complemento de 2
endmodule

module deMUX (
  input  [3:0] in_1,
  output a,
  output b,
  output c,
  output d,
  output e,
  output f,
  output g
);

  wire and_1_out, and_2_out, and_3_out, and_4_out, and_5_out, and_6_out, and_7_out, and_8_out, and_9_out,
       and_10_out, and_11_out, and_12_out, and_13_out, and_14_out, and_15_out, and_16_out, not_1_out,
       not_2_out, not_3_out, not_4_out, not_5_out, not_6_out, not_7_out, not_8_out, not_9_out, not_10_out,
       not_11_out, not_12_out, not_13_out, not_14_out, not_15_out, not_16_out, not_17_out, not_18_out,
       not_19_out, not_20_out, not_21_out;

  not not_1 (not_1_out, in_1[2]);
  not not_2 (not_2_out, in_1[0]);
  not not_3 (not_3_out, in_1[1]);
  not not_4 (not_4_out, in_1[0]);
  not not_5 (not_5_out, in_1[1]);
  not not_6 (not_6_out, in_1[2]);
  not not_7 (not_7_out, in_1[0]);
  not not_8 (not_8_out, in_1[2]);
  not not_9 (not_9_out, in_1[0]);
  not not_10 (not_10_out, in_1[1]);
  not not_11 (not_11_out, in_1[2]);
  not not_12 (not_12_out, in_1[0]);
  not not_13 (not_13_out, in_1[0]);
  not not_14 (not_14_out, in_1[1]);
  not not_15 (not_15_out, in_1[0]);
  not not_16 (not_16_out, in_1[1]);
  not not_17 (not_17_out, in_1[0]);
  not not_18 (not_18_out, in_1[2]);
  not not_19 (not_19_out, in_1[1]);
  not not_20 (not_20_out, in_1[0]);
  and and_1 (and_1_out, not_1_out, not_2_out);
  and and_2 (and_2_out, in_1[2], in_1[0]);
  not not_21 (not_21_out, in_1[2]);
  and and_3 (and_3_out, not_3_out, not_4_out);
  and and_4 (and_4_out, in_1[1], in_1[0]);
  or or_1 (c, not_5_out, in_1[0], in_1[2]);
  and and_5 (and_5_out, not_6_out, not_7_out);
  and and_6 (and_6_out, not_8_out, in_1[1]);
  and and_7 (and_7_out, in_1[1], not_9_out);
  and and_8 (and_8_out, in_1[2], not_10_out, in_1[0]);
  and and_9 (and_9_out, not_11_out, not_12_out);
  and and_10 (and_10_out, in_1[1], not_13_out);
  and and_11 (and_11_out, not_14_out, not_15_out);
  and and_12 (and_12_out, in_1[2], not_16_out);
  and and_13 (and_13_out, in_1[2], not_17_out);
  and and_14 (and_14_out, not_18_out, in_1[1]);
  and and_15 (and_15_out, in_1[2], not_19_out);
  and and_16 (and_16_out, in_1[2], not_20_out);
  or or_2 (a, and_1_out, in_1[1], and_2_out, in_1[3]);
  or or_3 (b, not_21_out, and_3_out, and_4_out);
  or or_4 (d, and_5_out, and_6_out, and_7_out, and_8_out, in_1[3]);
  or or_5 (e, and_9_out, and_10_out);
  or or_6 (f, and_11_out, and_12_out, and_13_out, in_1[3]);
  or or_7 (g, and_14_out, and_15_out, and_16_out, in_1[3]);
endmodule

module MUX (
  input  e0,
  input  e1,
  input  e2,
  input  e3,
  input  e4,
  input  e5,
  input  e6,
  input  e7,
  input  e8,
  input  e9,
  output b3,
  output b2,
  output b1,
  output b0
);

  or or_1 (b3, e9, e8);
  or or_2 (b2, e7, e6, e5, e4);
  or or_3 (b1, e7, e6, e3, e2);
  or or_4 (b0, e9, e7, e5, e3, e1);
endmodule

module somador_1bit (
  input  A,
  input  B,
  input  Cin,
  output Cout,
  output S
);

  wire and_1_out, and_2_out, and_3_out, xor_1_out;

  and and_1 (and_1_out, A, B);
  and and_2 (and_2_out, A, Cin);
  and and_3 (and_3_out, B, Cin);
  xor xor_1 (xor_1_out, A, B);
  xor xor_2 (S, xor_1_out, Cin);
  or or_1 (Cout, and_1_out, and_2_out, and_3_out);
endmodule

module deMUX_testado (
  input  [3:0] in_1
);

  wire demux_1_a, demux_1_b, demux_1_c, demux_1_d, demux_1_e, demux_1_f, demux_1_g;

  deMUX demux_1 (
    .in_1(in_1), .a(demux_1_a), .b(demux_1_b), .c(demux_1_c), .d(demux_1_d), .e(demux_1_e), .f(demux_1_f),
    .g(demux_1_g));
  _7_Segment_Display u_7_segment_display_1 (
    .g(demux_1_g), .f(demux_1_f), .a(demux_1_a), .b(demux_1_b), .e(demux_1_e), .d(demux_1_d), .c(demux_1_c));  // open: dp
endmodule
